// Logisim project ceshi.circ as structural Verilog: 1 circuit, main circuit main
module main (
  input  [3:0] in_1,
  output [3:0] out_2
);

  wire [2:0] ram_1_data;

  RAM #(.addrWidth(4), .dataWidth(3), .bus("separate")) ram_1 (
    .addr(4'b0101), .data(ram_1_data));  // open: din, str, sel, clk, ld, clr
  ROM #(.addrWidth(3), .dataWidth(4)) rom_1 (.addr(ram_1_data), .data(out_2));  // open: sel

  // Notes on the sheet:
  //   contents of rom_1 (hex, n*v repeats v):
  //   2 b c d 3 e 6 5
endmodule
