// Logisim project p0-CRC校验.circ as structural Verilog: 2 circuits, main circuit CRC
module CRC (
  input  [7:0] in_1,
  input  [3:0] in_2,
  output [10:0] out_3
);

  wire d, g, z, \模二除法器_1_out_10 , \模二除法器_1_out_11 , \模二除法器_1_out_12 , \模二除法器_2_out_10 , \模二除法器_2_out_11 ,
       \模二除法器_2_out_12 , \模二除法器_3_out_10 , \模二除法器_3_out_11 , \模二除法器_3_out_12 , \模二除法器_4_out_10 ,
       \模二除法器_4_out_11 , \模二除法器_4_out_12 , \模二除法器_5_out_10 , \模二除法器_5_out_11 , \模二除法器_5_out_12 ,
       \模二除法器_6_out_10 , \模二除法器_6_out_11 , \模二除法器_6_out_12 ;

  \模二除法器  \u_模二除法器_1  (
    .in_1(in_1[7]), .in_2(in_1[6]), .in_3(in_1[5]), .in_4(in_1[4]), .in_5(in_2[3]), .in_6(in_2[2]),
    .in_7(in_2[1]), .in_8(in_2[0]), .out_10(\模二除法器_1_out_10 ), .out_11(\模二除法器_1_out_11 ),
    .out_12(\模二除法器_1_out_12 ));  // open: out_9
  \模二除法器  \u_模二除法器_2  (
    .in_1(\模二除法器_1_out_10 ), .in_2(\模二除法器_1_out_11 ), .in_3(\模二除法器_1_out_12 ), .in_4(in_1[3]),
    .in_5(in_2[3]), .in_6(in_2[2]), .in_7(in_2[1]), .in_8(in_2[0]), .out_10(\模二除法器_2_out_10 ),
    .out_11(\模二除法器_2_out_11 ), .out_12(\模二除法器_2_out_12 ));  // open: out_9
  \模二除法器  \u_模二除法器_3  (
    .in_1(g), .in_2(z), .in_3(d), .in_4(1'b0), .in_5(in_2[3]), .in_6(in_2[2]), .in_7(in_2[1]),
    .in_8(in_2[0]), .out_10(\模二除法器_3_out_10 ), .out_11(\模二除法器_3_out_11 ), .out_12(\模二除法器_3_out_12 ));  // open: out_9
  \模二除法器  \u_模二除法器_4  (
    .in_1(\模二除法器_2_out_10 ), .in_2(\模二除法器_2_out_11 ), .in_3(\模二除法器_2_out_12 ), .in_4(in_1[2]),
    .in_5(in_2[3]), .in_6(in_2[2]), .in_7(in_2[1]), .in_8(in_2[0]), .out_10(\模二除法器_4_out_10 ),
    .out_11(\模二除法器_4_out_11 ), .out_12(\模二除法器_4_out_12 ));  // open: out_9
  \模二除法器  \u_模二除法器_5  (
    .in_1(\模二除法器_3_out_10 ), .in_2(\模二除法器_3_out_11 ), .in_3(\模二除法器_3_out_12 ), .in_4(1'b0), .in_5(in_2[3]),
    .in_6(in_2[2]), .in_7(in_2[1]), .in_8(in_2[0]), .out_10(\模二除法器_5_out_10 ), .out_11(\模二除法器_5_out_11 ),
    .out_12(\模二除法器_5_out_12 ));  // open: out_9
  \模二除法器  \u_模二除法器_6  (
    .in_1(\模二除法器_4_out_10 ), .in_2(\模二除法器_4_out_11 ), .in_3(\模二除法器_4_out_12 ), .in_4(in_1[1]),
    .in_5(in_2[3]), .in_6(in_2[2]), .in_7(in_2[1]), .in_8(in_2[0]), .out_10(\模二除法器_6_out_10 ),
    .out_11(\模二除法器_6_out_11 ), .out_12(\模二除法器_6_out_12 ));  // open: out_9
  \模二除法器  \u_模二除法器_7  (
    .in_1(\模二除法器_5_out_10 ), .in_2(\模二除法器_5_out_11 ), .in_3(\模二除法器_5_out_12 ), .in_4(1'b0), .in_5(in_2[3]),
    .in_6(in_2[2]), .in_7(in_2[1]), .in_8(in_2[0]), .out_10(out_3[2]), .out_11(out_3[1]), .out_12(out_3[0]));  // open: out_9
  \模二除法器  \u_模二除法器_8  (
    .in_1(\模二除法器_6_out_10 ), .in_2(\模二除法器_6_out_11 ), .in_3(\模二除法器_6_out_12 ), .in_4(in_1[0]),
    .in_5(in_2[3]), .in_6(in_2[2]), .in_7(in_2[1]), .in_8(in_2[0]), .out_10(g), .out_11(z), .out_12(d));  // open: out_9

  assign out_3[10:3] = in_1;

  // Other names for the same wires on the sheet: _0 = in_2[0]; _1 = in_2[1]; _2 = in_2[2]; _3 = in_2[3];
  //   bb[2:0] = out_3[2:0]; aa[7:0] = in_1
endmodule

module \模二除法器  (
  input  in_1,
  input  in_2,
  input  in_3,
  input  in_4,
  input  in_5,
  input  in_6,
  input  in_7,
  input  in_8,
  output out_9,
  output out_10,
  output out_11,
  output out_12
);

  wire xor_1_out, xor_2_out, xor_3_out;

  xor xor_1 (xor_1_out, in_2, in_6);
  xor xor_2 (xor_2_out, in_3, in_7);
  xor xor_3 (xor_3_out, in_4, in_8);
  Multiplexer multiplexer_1 (.in0(in_2), .in1(xor_1_out), .out(out_10), .sel(in_1));  // open: en
  Multiplexer multiplexer_2 (.in0(in_3), .in1(xor_2_out), .out(out_11), .sel(in_1));  // open: en
  Multiplexer multiplexer_3 (.in0(in_4), .in1(xor_3_out), .out(out_12), .sel(in_1));  // open: en

  assign out_9 = in_1;
endmodule
