// Logisim project p0-FSM.circ as structural Verilog: 4 circuits, main circuit fsm
module fsm (
  input  in_1,
  input  [1:0] in_2,
  output out_3
);

  wire clock_1_out;
  wire [1:0] multiplexer_1_out, register_1_q, zi_1_y;

  zi zi_1 (.a(in_2[1]), .b(in_2[0]), .c(register_1_q[1]), .d(register_1_q[0]), .x(zi_1_y[1]), .y(zi_1_y[0]));
  Multiplexer #(.width(2), .enable("false")) multiplexer_1 (
    .in0(zi_1_y), .in1(2'b00), .out(multiplexer_1_out), .sel(in_1));
  Register #(.width(2)) register_1 (.D(multiplexer_1_out), .Q(register_1_q), .clk(clock_1_out));  // open: en, clr
  Clock clock_1 (.out(clock_1_out));
  out out_1 (.a(in_2[1]), .b(in_2[0]), .c(register_1_q[1]), .d(register_1_q[0]), .e(out_3));

  // Other names for the same wires on the sheet: clr = in_1
endmodule

module zi (
  input  a,
  input  b,
  input  c,
  input  d,
  output x,
  output y
);

  wire and_1_out, and_2_out, and_3_out, and_4_out, not_1_out, not_2_out, not_3_out, not_4_out, not_5_out,
       not_6_out, not_7_out;

  not not_1 (not_1_out, b);
  and and_1 (and_1_out, not_1_out, not_2_out, d);
  not not_2 (not_2_out, c);
  not not_3 (not_3_out, b);
  and and_2 (and_2_out, not_3_out, c, not_4_out);
  not not_4 (not_4_out, d);
  not not_5 (not_5_out, b);
  and and_3 (and_3_out, not_5_out, c, not_6_out);
  not not_6 (not_6_out, d);
  not not_7 (not_7_out, a);
  and and_4 (and_4_out, not_7_out, b);
  or or_1 (x, and_1_out, and_2_out);
  or or_2 (y, and_3_out, and_4_out);
endmodule

module out (
  input  a,
  input  b,
  input  c,
  input  d,
  output e
);

  wire not_1_out, not_2_out;

  not not_1 (not_1_out, b);
  and and_1 (e, not_1_out, c, not_2_out);
  not not_2 (not_2_out, d);
endmodule

module ceshi (
);

  wire clock_1_out, fsm_1_out_3;
  wire [2:0] rom_1_data;
  wire [7:0] counter_1_q;

  Counter counter_1 (.Q(counter_1_q), .clk(clock_1_out));  // open: load, D, count, carry, clr
  Clock clock_1 (.out(clock_1_out));
  ROM #(.dataWidth(3)) rom_1 (.addr(counter_1_q), .data(rom_1_data));  // open: sel
  fsm fsm_1 (.in_1(rom_1_data[0]), .in_2(rom_1_data[2:1]), .out_3(fsm_1_out_3));
  // Probe on rom_1_data[0]
  // Probe on rom_1_data[2:1]
  // Probe on fsm_1_out_3

  // Notes on the sheet:
  //   contents of rom_1 (hex, n*v repeats v):
  //   7 7 4 2 7 7 7 4 6 4*2 6 4 6 2 4 5 5 5 1 4 1 3 6 4 1 3 5 6 5 3 2 5 6 5 5 4 1 3 2 5 6 5 3 5 5 4 5 5 5
  //   3 4 5 2 4 4 4 5 3 7 7 2 2 7 3 7 2 4 5 3 4 6 3 1 6 6 2 4
endmodule
