// Logisim project p0-GRF.circ as structural Verilog: 1 circuit, main circuit grf
module grf (
  input  clk,
  input  reset,
  input  WE,
  input  [4:0] A1,
  input  [4:0] A2,
  input  [4:0] A3,
  input  [31:0] WD,
  output [31:0] RD1,
  output [31:0] RD2
);

  wire EN1, EN2, EN3, EN4, EN5, EN6, EN7, EN8, EN9, EN10, EN11, EN12, EN13, EN14, EN15, EN16, EN17, EN18,
       EN19, EN20, EN21, EN22, EN23, EN24, EN25, EN26, EN27, EN28, EN29, EN30, EN31, EN32;
  wire [31:0] in1, in2, in3, in4, in5, in6, in7, in8, in9, in10, in11, in12, in13, in14, in15, in16, in17,
       in18, in19, in20, in21, in22, in23, in24, in25, in26, in27, in28, in29, in30, in31, in32, out1, out2,
       out3, out4, out5, out6, out7, out8, out9, out10, out11, out12, out13, out14, out15, out16, out17,
       out18, out19, out20, out21, out22, out23, out24, out25, out26, out27, out28, out29, out30, out31,
       out32;

  Register #(.width(32)) register_1 (.D(in1), .en(EN1), .Q(out1), .clk(clk), .clr(reset));
  Register #(.width(32)) register_2 (.D(in9), .en(EN9), .Q(out9), .clk(clk), .clr(reset));
  Register #(.width(32)) register_3 (.D(in17), .en(EN17), .Q(out17), .clk(clk), .clr(reset));
  Register #(.width(32)) register_4 (.D(in25), .en(EN25), .Q(out25), .clk(clk), .clr(reset));
  Demultiplexer #(.select(5), .width(32)) demultiplexer_1 (
    .out1(in2), .out2(in3), .out3(in4), .out4(in5), .out5(in6), .out6(in7), .out7(in8), .out8(in9),
    .out9(in10), .out10(in11), .out11(in12), .out12(in13), .out13(in14), .out14(in15), .out15(in16),
    .out16(in17), .out17(in18), .out18(in19), .out19(in20), .out20(in21), .out21(in22), .out22(in23),
    .out23(in24), .out24(in25), .out25(in26), .out26(in27), .out27(in28), .out28(in29), .out29(in30),
    .out30(in31), .out31(in32), .in(WD), .sel(A3));  // open: out0, en
  Register #(.width(32)) register_5 (.D(in2), .en(EN2), .Q(out2), .clk(clk), .clr(reset));
  Register #(.width(32)) register_6 (.D(in10), .en(EN10), .Q(out10), .clk(clk), .clr(reset));
  Register #(.width(32)) register_7 (.D(in18), .en(EN18), .Q(out18), .clk(clk), .clr(reset));
  Register #(.width(32)) register_8 (.D(in26), .en(EN26), .Q(out26), .clk(clk), .clr(reset));
  Register #(.width(32)) register_9 (.D(in3), .en(EN3), .Q(out3), .clk(clk), .clr(reset));
  Register #(.width(32)) register_10 (.D(in11), .en(EN11), .Q(out11), .clk(clk), .clr(reset));
  Register #(.width(32)) register_11 (.D(in19), .en(EN19), .Q(out19), .clk(clk), .clr(reset));
  Register #(.width(32)) register_12 (.D(in27), .en(EN27), .Q(out27), .clk(clk), .clr(reset));
  Register #(.width(32)) register_13 (.D(in4), .en(EN4), .Q(out4), .clk(clk), .clr(reset));
  Register #(.width(32)) register_14 (.D(in12), .en(EN12), .Q(out12), .clk(clk), .clr(reset));
  Register #(.width(32)) register_15 (.D(in20), .en(EN20), .Q(out20), .clk(clk), .clr(reset));
  Register #(.width(32)) register_16 (.D(in28), .en(EN28), .Q(out28), .clk(clk), .clr(reset));
  Register #(.width(32)) register_17 (.D(in5), .en(EN5), .Q(out5), .clk(clk), .clr(reset));
  Register #(.width(32)) register_18 (.D(in13), .en(EN13), .Q(out13), .clk(clk), .clr(reset));
  Register #(.width(32)) register_19 (.D(in21), .en(EN21), .Q(out21), .clk(clk), .clr(reset));
  Register #(.width(32)) register_20 (.D(in29), .en(EN29), .Q(out29), .clk(clk), .clr(reset));
  Register #(.width(32)) register_21 (.D(in6), .en(EN6), .Q(out6), .clk(clk), .clr(reset));
  Register #(.width(32)) register_22 (.D(in14), .en(EN14), .Q(out14), .clk(clk), .clr(reset));
  Register #(.width(32)) register_23 (.D(in22), .en(EN22), .Q(out22), .clk(clk), .clr(reset));
  Register #(.width(32)) register_24 (.D(in30), .en(EN30), .Q(out30), .clk(clk), .clr(reset));
  Demultiplexer #(.select(5)) demultiplexer_2 (
    .out0(EN1), .out1(EN2), .out2(EN3), .out3(EN4), .out4(EN5), .out5(EN6), .out6(EN7), .out7(EN8),
    .out8(EN9), .out9(EN10), .out10(EN11), .out11(EN12), .out12(EN13), .out13(EN14), .out14(EN15),
    .out15(EN16), .out16(EN17), .out17(EN18), .out18(EN19), .out19(EN20), .out20(EN21), .out21(EN22),
    .out22(EN23), .out23(EN24), .out24(EN25), .out25(EN26), .out26(EN27), .out27(EN28), .out28(EN29),
    .out29(EN30), .out30(EN31), .out31(EN32), .in(WE), .sel(A3));  // open: en
  Register #(.width(32)) register_25 (.D(in7), .en(EN7), .Q(out7), .clk(clk), .clr(reset));
  Register #(.width(32)) register_26 (.D(in15), .en(EN15), .Q(out15), .clk(clk), .clr(reset));
  Register #(.width(32)) register_27 (.D(in23), .en(EN23), .Q(out23), .clk(clk), .clr(reset));
  Register #(.width(32)) register_28 (.D(in31), .en(EN31), .Q(out31), .clk(clk), .clr(reset));
  Register #(.width(32)) register_29 (.D(in8), .en(EN8), .Q(out8), .clk(clk), .clr(reset));
  Register #(.width(32)) register_30 (.D(in16), .en(EN16), .Q(out16), .clk(clk), .clr(reset));
  Register #(.width(32)) register_31 (.D(in24), .en(EN24), .Q(out24), .clk(clk), .clr(reset));
  Register #(.width(32)) register_32 (.D(in32), .en(EN32), .Q(out32), .clk(clk), .clr(reset));
  Multiplexer #(.select(5), .width(32)) multiplexer_1 (
    .in0({32{1'b0}}), .in1(out2), .in2(out3), .in3(out4), .in4(out5), .in5(out6), .in6(out7), .in7(out8),
    .in8(out9), .in9(out10), .in10(out11), .in11(out12), .in12(out13), .in13(out14), .in14(out15),
    .in15(out16), .in16(out17), .in17(out18), .in18(out19), .in19(out20), .in20(out21), .in21(out22),
    .in22(out23), .in23(out24), .in24(out25), .in25(out26), .in26(out27), .in27(out28), .in28(out29),
    .in29(out30), .in30(out31), .in31(out32), .out(RD1), .sel(A1));  // open: en
  Multiplexer #(.select(5), .width(32)) multiplexer_2 (
    .in0({32{1'b0}}), .in1(out2), .in2(out3), .in3(out4), .in4(out5), .in5(out6), .in6(out7), .in7(out8),
    .in8(out9), .in9(out10), .in10(out11), .in11(out12), .in12(out13), .in13(out14), .in14(out15),
    .in15(out16), .in16(out17), .in17(out18), .in18(out19), .in19(out20), .in20(out21), .in21(out22),
    .in22(out23), .in23(out24), .in24(out25), .in25(out26), .in26(out27), .in27(out28), .in28(out29),
    .in29(out30), .in30(out31), .in31(out32), .out(RD2), .sel(A2));  // open: en

  // Other names for the same wires on the sheet: EN = WE; shuru[31:0] = WD
endmodule
