// Logisim project swap未完成.circ as structural Verilog: 1 circuit, main circuit main
module main (
  input  in_1,
  input  in_2,
  input  in_3,
  output out_4,
  output out_5
);

  wire and_1_out, xor_1_out, xor_2_out, xor_3_out;

  xor xor_1 (xor_1_out, in_1, in_2);
  and and_1 (and_1_out, xor_1_out, in_3);
  xor xor_2 (xor_2_out, in_1, xor_1_out);
  xor xor_3 (xor_3_out, xor_1_out, in_2);
  // AND_Gate and_2 has open pins: in1=xor_2_out, in2=and_1_out, out=open
  // AND_Gate and_3 has open pins: in1=xor_3_out, in2=and_1_out, out=open
endmodule
