// Logisim project 单周期CPU升级.circ as structural Verilog: 8 circuits, main circuit main
module main (
  input  reset,
  output [31:0] out_2,
  output out_3,
  output [4:0] out_4,
  output [31:0] out_5,
  output out_6,
  output [4:0] out_7,
  output [31:0] out_8
);

  wire ALUSrc, Branch_Enable, clock_1_out, PcSrc, RegDst, RegIn, Rst, Shift2, SiExt;
  wire [1:0] alu_1_result;
  wire [3:0] ALUOP;
  wire [24:0] alu_1_result_2;
  wire [31:0] bit_extender_1_out, bit_extender_2_out, GRF_rd1, multiplexer_1_out, multiplexer_3_out,
       multiplexer_4_out, multiplexer_5_out, ram_1_data, shifter_1_out;

  // Probe on out_2[31:26]
  Clock clock_1 (.out(clock_1_out));
  // Probe on out_2[5:0]
  IFU IFU (
    .If_Branch(PcSrc), .immediate(multiplexer_3_out), .clk(clock_1_out), .reset(reset), .out_6(out_2),
    .Branch_Enable(Branch_Enable));  // open: out_7
  // Probe on out_2
  assign bit_extender_1_out = {{16{1'b0}}, out_2[15:0]};  // Bit_Extender bit_extender_1
  assign bit_extender_2_out = {{16{out_2[15]}}, out_2[15:0]};  // Bit_Extender bit_extender_2
  Multiplexer #(.width(32), .enable("false")) multiplexer_1 (
    .in0(bit_extender_1_out), .in1(bit_extender_2_out), .out(multiplexer_1_out), .sel(SiExt));
  controller controller_1 (
    .instr(out_2), .RegDst(RegDst), .SiExt(SiExt), .Shift2(Shift2), .RegWrite(out_3), .Rst(Rst),
    .ALUSrc(ALUSrc), .RegIn(RegIn), .MemWrite(out_6), .Branch_Enable(Branch_Enable), .ALUOP(ALUOP));
  Shifter #(.width(32)) shifter_1 (.in(multiplexer_1_out), .\dist (5'b00010), .out(shifter_1_out));
  Multiplexer #(.width(5), .enable("false")) multiplexer_2 (
    .in0(out_2[15:11]), .in1(out_2[20:16]), .out(out_4), .sel(RegDst));
  Multiplexer #(.width(32), .enable("false")) multiplexer_3 (
    .in0(multiplexer_1_out), .in1(shifter_1_out), .out(multiplexer_3_out), .sel(Shift2));
  GRF GRF (
    .clk(clock_1_out), .reset(reset), .WE(out_3), .A1(out_2[25:21]), .A2(out_2[20:16]), .A3(out_4),
    .WD(out_5), .RD1(GRF_rd1), .RD2(out_8));
  Multiplexer #(.width(32), .enable("false")) multiplexer_4 (
    .in0(GRF_rd1), .in1(out_8), .out(multiplexer_4_out), .sel(Rst));
  Multiplexer #(.width(32), .enable("false")) multiplexer_5 (
    .in0(out_8), .in1(multiplexer_3_out), .out(multiplexer_5_out), .sel(ALUSrc));
  ALU alu_1 (
    .in_1(multiplexer_4_out), .in_2(multiplexer_5_out), .ALUOP(ALUOP), .Branch(PcSrc),
    .Result({alu_1_result_2, out_7, alu_1_result}));
  Multiplexer #(.width(32), .enable("false")) multiplexer_6 (
    .in0({alu_1_result_2, out_7, alu_1_result}), .in1(ram_1_data), .out(out_5), .sel(RegIn));
  // Probe on ram_1_data
  RAM #(.addrWidth(5), .dataWidth(32), .bus("separate")) ram_1 (
    .addr(out_7), .din(out_8), .data(ram_1_data), .str(out_6), .clk(clock_1_out), .clr(reset));  // open: sel, ld

  // Other names for the same wires on the sheet: Memaddr[4:0] = out_7; _1 = out_2[0]; immediate16[15:0] = out_2[15:0];
  //   Instr[31:0] = out_2; _2 = out_2[1]; _3 = out_2[2]; _4 = out_2[3]; _5 = out_2[4]; _6 = out_2[5]; _12 = out_2[11];
  //   RD[4:0] = out_2[15:11]; _13 = out_2[12]; _14 = out_2[13]; _15 = out_2[14]; _16 = out_2[15]; _27 = out_2[26];
  //   _28 = out_2[27]; _29 = out_2[28]; _30 = out_2[29]; _31 = out_2[30]; _32 = out_2[31]; Memdata[31:0] = out_8;
  //   MemWrite = out_6; regaddr[4:0] = out_4; regdata[31:0] = out_5; RegWrite = out_3; _22 = out_2[21];
  //   RS[4:0] = out_2[25:21]; _23 = out_2[22]; _24 = out_2[23]; _25 = out_2[24]; _26 = out_2[25]; _17 = out_2[16];
  //   RT[4:0] = out_2[20:16]; _18 = out_2[17]; _19 = out_2[18]; _20 = out_2[19]; _21 = out_2[20]; _7 = out_2[6];
  //   Shamt[4:0] = out_2[10:6]; _8 = out_2[7]; _9 = out_2[8]; _10 = out_2[9]; _11 = out_2[10]
endmodule

module GRF (
  input  clk,
  input  reset,
  input  WE,
  input  [4:0] A1,
  input  [4:0] A2,
  input  [4:0] A3,
  input  [31:0] WD,
  output [31:0] RD1,
  output [31:0] RD2
);

  wire EN2, EN3, EN4, EN5, EN6, EN7, EN8, EN9, EN10, EN11, EN12, EN13, EN14, EN15, EN16, EN17, EN18, EN19,
       EN20, EN21, EN22, EN23, EN24, EN25, EN26, EN27, EN28, EN29, EN30, EN31, EN32;
  wire [31:0] in1, in2, in3, in4, in5, in6, in7, in8, in9, in10, in11, in12, in13, in14, in15, in16, in17,
       in18, in19, in20, in21, in22, in23, in24, in25, in26, in27, in28, in29, in30, in31, in32, out1, out2,
       out3, out4, out5, out6, out7, out8, out9, out10, out11, out12, out13, out14, out15, out16, out17,
       out18, out19, out20, out21, out22, out23, out24, out25, out26, out27, out28, out29, out30, out31,
       out32;

  Register #(.width(32)) register_1 (.D(in1), .en(1'b0), .Q(out1), .clk(clk), .clr(reset));
  Register #(.width(32)) register_2 (.D(in9), .en(EN9), .Q(out9), .clk(clk), .clr(reset));
  Register #(.width(32)) register_3 (.D(in17), .en(EN17), .Q(out17), .clk(clk), .clr(reset));
  Register #(.width(32)) register_4 (.D(in25), .en(EN25), .Q(out25), .clk(clk), .clr(reset));
  Demultiplexer #(.select(5), .width(32)) demultiplexer_1 (
    .out0(in1), .out1(in2), .out2(in3), .out3(in4), .out4(in5), .out5(in6), .out6(in7), .out7(in8),
    .out8(in9), .out9(in10), .out10(in11), .out11(in12), .out12(in13), .out13(in14), .out14(in15),
    .out15(in16), .out16(in17), .out17(in18), .out18(in19), .out19(in20), .out20(in21), .out21(in22),
    .out22(in23), .out23(in24), .out24(in25), .out25(in26), .out26(in27), .out27(in28), .out28(in29),
    .out29(in30), .out30(in31), .out31(in32), .in(WD), .sel(A3));  // open: en
  Register #(.width(32)) register_5 (.D(in2), .en(EN2), .Q(out2), .clk(clk), .clr(reset));
  Register #(.width(32)) register_6 (.D(in10), .en(EN10), .Q(out10), .clk(clk), .clr(reset));
  Register #(.width(32)) register_7 (.D(in18), .en(EN18), .Q(out18), .clk(clk), .clr(reset));
  Register #(.width(32)) register_8 (.D(in26), .en(EN26), .Q(out26), .clk(clk), .clr(reset));
  Register #(.width(32)) register_9 (.D(in3), .en(EN3), .Q(out3), .clk(clk), .clr(reset));
  Register #(.width(32)) register_10 (.D(in11), .en(EN11), .Q(out11), .clk(clk), .clr(reset));
  Register #(.width(32)) register_11 (.D(in19), .en(EN19), .Q(out19), .clk(clk), .clr(reset));
  Register #(.width(32)) register_12 (.D(in27), .en(EN27), .Q(out27), .clk(clk), .clr(reset));
  Register #(.width(32)) register_13 (.D(in4), .en(EN4), .Q(out4), .clk(clk), .clr(reset));
  Register #(.width(32)) register_14 (.D(in12), .en(EN12), .Q(out12), .clk(clk), .clr(reset));
  Register #(.width(32)) register_15 (.D(in20), .en(EN20), .Q(out20), .clk(clk), .clr(reset));
  Register #(.width(32)) register_16 (.D(in28), .en(EN28), .Q(out28), .clk(clk), .clr(reset));
  Register #(.width(32)) register_17 (.D(in5), .en(EN5), .Q(out5), .clk(clk), .clr(reset));
  Register #(.width(32)) register_18 (.D(in13), .en(EN13), .Q(out13), .clk(clk), .clr(reset));
  Register #(.width(32)) register_19 (.D(in21), .en(EN21), .Q(out21), .clk(clk), .clr(reset));
  Register #(.width(32)) register_20 (.D(in29), .en(EN29), .Q(out29), .clk(clk), .clr(reset));
  Register #(.width(32)) register_21 (.D(in6), .en(EN6), .Q(out6), .clk(clk), .clr(reset));
  Register #(.width(32)) register_22 (.D(in14), .en(EN14), .Q(out14), .clk(clk), .clr(reset));
  Register #(.width(32)) register_23 (.D(in22), .en(EN22), .Q(out22), .clk(clk), .clr(reset));
  Register #(.width(32)) register_24 (.D(in30), .en(EN30), .Q(out30), .clk(clk), .clr(reset));
  Demultiplexer #(.select(5)) demultiplexer_2 (
    .out1(EN2), .out2(EN3), .out3(EN4), .out4(EN5), .out5(EN6), .out6(EN7), .out7(EN8), .out8(EN9),
    .out9(EN10), .out10(EN11), .out11(EN12), .out12(EN13), .out13(EN14), .out14(EN15), .out15(EN16),
    .out16(EN17), .out17(EN18), .out18(EN19), .out19(EN20), .out20(EN21), .out21(EN22), .out22(EN23),
    .out23(EN24), .out24(EN25), .out25(EN26), .out26(EN27), .out27(EN28), .out28(EN29), .out29(EN30),
    .out30(EN31), .out31(EN32), .in(WE), .sel(A3));  // open: out0, en
  Register #(.width(32)) register_25 (.D(in7), .en(EN7), .Q(out7), .clk(clk), .clr(reset));
  Register #(.width(32)) register_26 (.D(in15), .en(EN15), .Q(out15), .clk(clk), .clr(reset));
  Register #(.width(32)) register_27 (.D(in23), .en(EN23), .Q(out23), .clk(clk), .clr(reset));
  Register #(.width(32)) register_28 (.D(in31), .en(EN31), .Q(out31), .clk(clk), .clr(reset));
  Register #(.width(32)) register_29 (.D(in8), .en(EN8), .Q(out8), .clk(clk), .clr(reset));
  Register #(.width(32)) register_30 (.D(in16), .en(EN16), .Q(out16), .clk(clk), .clr(reset));
  Register #(.width(32)) register_31 (.D(in24), .en(EN24), .Q(out24), .clk(clk), .clr(reset));
  Register #(.width(32)) register_32 (.D(in32), .en(EN32), .Q(out32), .clk(clk), .clr(reset));
  Multiplexer #(.select(5), .width(32)) multiplexer_1 (
    .in0({32{1'b0}}), .in1(out2), .in2(out3), .in3(out4), .in4(out5), .in5(out6), .in6(out7), .in7(out8),
    .in8(out9), .in9(out10), .in10(out11), .in11(out12), .in12(out13), .in13(out14), .in14(out15),
    .in15(out16), .in16(out17), .in17(out18), .in18(out19), .in19(out20), .in20(out21), .in21(out22),
    .in22(out23), .in23(out24), .in24(out25), .in25(out26), .in26(out27), .in27(out28), .in28(out29),
    .in29(out30), .in30(out31), .in31(out32), .out(RD1), .sel(A1));  // open: en
  Multiplexer #(.select(5), .width(32)) multiplexer_2 (
    .in0({32{1'b0}}), .in1(out2), .in2(out3), .in3(out4), .in4(out5), .in5(out6), .in6(out7), .in7(out8),
    .in8(out9), .in9(out10), .in10(out11), .in11(out12), .in12(out13), .in13(out14), .in14(out15),
    .in15(out16), .in16(out17), .in17(out18), .in18(out19), .in19(out20), .in20(out21), .in21(out22),
    .in22(out23), .in23(out24), .in24(out25), .in25(out26), .in26(out27), .in27(out28), .in28(out29),
    .in29(out30), .in30(out31), .in31(out32), .out(RD2), .sel(A2));  // open: en

  // Other names for the same wires on the sheet: EN = WE; shuru[31:0] = WD
endmodule

module IFU (
  input  [31:0] immediate,
  input  If_Branch,
  input  Branch_Enable,
  input  clk,
  input  reset,
  output [31:0] out_6,
  output [31:0] out_7
);

  wire and_1_out;
  wire [31:0] adder_1_out, adder_2_out, multiplexer_1_out;

  Adder #(.width(32)) adder_1 (.a(adder_2_out), .b(immediate), .out(adder_1_out));  // open: cin, cout
  Multiplexer #(.width(32), .enable("false")) multiplexer_1 (
    .in0(adder_2_out), .in1(adder_1_out), .out(multiplexer_1_out), .sel(and_1_out));
  and and_1 (and_1_out, If_Branch, Branch_Enable);
  Register #(.width(32)) PC (.D(multiplexer_1_out), .Q(out_7), .clk(clk), .clr(reset));  // open: en
  Adder #(.width(32)) adder_2 (.a(32'h4), .b(out_7), .out(adder_2_out));  // open: cin, cout
  ROM #(.addrWidth(5), .dataWidth(32)) rom_1 (.addr(out_7[6:2]), .data(out_6));  // open: sel

  // Notes on the sheet:
  //   contents of rom_1 (hex, n*v repeats v):
  //   341c0000 341d0000 340080f8 36ee0367 3593769c 34dda539 3465c5dc 34be0ff1 3472af1d 35566602 35fe72a7
  //   3437ff23 37b9649e 3690bf9b 37fe4e0c 3711f49d 3c113bfe 3c057433 3c03c451 3c04c431 3c1c24d9 3c1bf0da
  //   3c0ccc68 3c0a118d 3c1021ea 3c0004d3 3c16115b 3c184f06 3c1215de 1000ffff
endmodule

module controller (
  input  [31:0] instr,
  output RegDst,
  output SiExt,
  output Shift2,
  output RegWrite,
  output Rst,
  output ALUSrc,
  output RegIn,
  output MemWrite,
  output Branch_Enable,
  output [3:0] ALUOP
);

  wire and_logic_1_addiu, and_logic_1_addu, and_logic_1_and, and_logic_1_andi, and_logic_1_beq,
       and_logic_1_bgez, and_logic_1_bgtz, and_logic_1_blez, and_logic_1_bltz, and_logic_1_bne,
       and_logic_1_lui, and_logic_1_lw, and_logic_1_or, and_logic_1_ori, and_logic_1_subu, and_logic_1_sw,
       and_logic_1_xor, and_logic_1_xori;

  and_logic and_logic_1 (
    .instr(instr), .addu(and_logic_1_addu), .addiu(and_logic_1_addiu), .\and (and_logic_1_and),
    .andi(and_logic_1_andi), .subu(and_logic_1_subu), .\or (and_logic_1_or), .ori(and_logic_1_ori),
    .\xor (and_logic_1_xor), .xori(and_logic_1_xori), .lui(and_logic_1_lui), .lw(and_logic_1_lw),
    .sw(and_logic_1_sw), .beq(and_logic_1_beq), .bgez(and_logic_1_bgez), .bgtz(and_logic_1_bgtz),
    .blez(and_logic_1_blez), .bltz(and_logic_1_bltz), .bne(and_logic_1_bne));
  or_logic Or_Logic (
    .addu(and_logic_1_addu), .addiu(and_logic_1_addiu), .\and (and_logic_1_and), .andi(and_logic_1_andi),
    .subu(and_logic_1_subu), .\or (and_logic_1_or), .ori(and_logic_1_ori), .\xor (and_logic_1_xor),
    .xori(and_logic_1_xori), .lui(and_logic_1_lui), .lw(and_logic_1_lw), .sw(and_logic_1_sw),
    .beq(and_logic_1_beq), .bgez(and_logic_1_bgez), .bgtz(and_logic_1_bgtz), .blez(and_logic_1_blez),
    .bltz(and_logic_1_bltz), .bne(and_logic_1_bne), .RegDst(RegDst), .SiExt(SiExt), .Shift2(Shift2),
    .RegWrite(RegWrite), .Rst(Rst), .ALUSrc(ALUSrc), .RegIn(RegIn), .MemWrite(MemWrite),
    .Branch_Enable(Branch_Enable), .ALU3(ALUOP[3]), .ALU2(ALUOP[2]), .ALU1(ALUOP[1]), .ALU0(ALUOP[0]));
endmodule

module and_logic (
  input  [31:0] instr,
  output addu,
  output addiu,
  output \and ,
  output andi,
  output subu,
  output \or ,
  output ori,
  output \xor ,
  output xori,
  output lui,
  output lw,
  output sw,
  output beq,
  output bgez,
  output bgtz,
  output blez,
  output bltz,
  output bne
);

  wire and_2_out, and_4_out, and_6_out, and_7_out, and_9_out, and_15_out, and_16_out, and_19_out, and_20_out,
       not_1_out, not_2_out, not_3_out, not_4_out, not_5_out, not_6_out, not_7_out, not_8_out, not_9_out,
       not_10_out, not_11_out, not_12_out, not_13_out, not_14_out, not_15_out, not_16_out, not_17_out,
       not_18_out, not_19_out, not_20_out, not_21_out, not_22_out, not_23_out, not_24_out, not_25_out,
       not_26_out, not_27_out, not_28_out, not_29_out, not_30_out, not_31_out, not_32_out, not_33_out,
       not_34_out, not_35_out, not_36_out, not_37_out, not_38_out, not_39_out, not_40_out, not_41_out,
       not_42_out, not_43_out, not_44_out, not_45_out, not_46_out, not_47_out, not_48_out, not_49_out,
       not_50_out, not_51_out, not_52_out, not_53_out, not_54_out, not_55_out, not_56_out, not_57_out,
       not_58_out, not_59_out, not_60_out, not_61_out, not_62_out, not_63_out, not_64_out, not_65_out,
       not_66_out, not_67_out, not_68_out, not_69_out, not_70_out, not_71_out, not_72_out, not_73_out,
       not_74_out, not_75_out, not_76_out, not_77_out, not_78_out, not_79_out, opis0;

  not not_1 (not_1_out, instr[31]);
  not not_2 (not_2_out, instr[30]);
  not not_3 (not_3_out, instr[29]);
  not not_4 (not_4_out, instr[28]);
  not not_5 (not_5_out, instr[27]);
  not not_6 (not_6_out, instr[26]);
  and and_1 (opis0, not_1_out, not_2_out, not_3_out, not_4_out, not_5_out, not_6_out);
  not not_7 (not_7_out, instr[4]);
  not not_8 (not_8_out, instr[3]);
  not not_9 (not_9_out, instr[2]);
  not not_10 (not_10_out, instr[1]);
  not not_11 (not_11_out, instr[5]);
  not not_12 (not_12_out, instr[4]);
  not not_13 (not_13_out, instr[2]);
  not not_14 (not_14_out, instr[1]);
  not not_15 (not_15_out, instr[4]);
  not not_16 (not_16_out, instr[3]);
  not not_17 (not_17_out, instr[1]);
  not not_18 (not_18_out, instr[0]);
  not not_19 (not_19_out, instr[31]);
  not not_20 (not_20_out, instr[30]);
  not not_21 (not_21_out, instr[27]);
  not not_22 (not_22_out, instr[26]);
  not not_23 (not_23_out, instr[4]);
  not not_24 (not_24_out, instr[3]);
  not not_25 (not_25_out, instr[2]);
  not not_26 (not_26_out, instr[4]);
  not not_27 (not_27_out, instr[3]);
  not not_28 (not_28_out, instr[1]);
  not not_29 (not_29_out, instr[31]);
  not not_30 (not_30_out, instr[30]);
  not not_31 (not_31_out, instr[27]);
  not not_32 (not_32_out, instr[4]);
  not not_33 (not_33_out, instr[3]);
  not not_34 (not_34_out, instr[0]);
  not not_35 (not_35_out, instr[31]);
  not not_36 (not_36_out, instr[30]);
  not not_37 (not_37_out, instr[26]);
  not not_38 (not_38_out, instr[31]);
  not not_39 (not_39_out, instr[30]);
  not not_40 (not_40_out, instr[30]);
  not not_41 (not_41_out, instr[29]);
  not not_42 (not_42_out, instr[28]);
  not not_43 (not_43_out, instr[30]);
  not not_44 (not_44_out, instr[28]);
  not not_45 (not_45_out, instr[31]);
  not not_46 (not_46_out, instr[30]);
  not not_47 (not_47_out, instr[29]);
  not not_48 (not_48_out, instr[27]);
  not not_49 (not_49_out, instr[26]);
  not not_50 (not_50_out, instr[31]);
  not not_51 (not_51_out, instr[30]);
  not not_52 (not_52_out, instr[29]);
  not not_53 (not_53_out, instr[28]);
  not not_54 (not_54_out, instr[27]);
  not not_55 (not_55_out, instr[20]);
  not not_56 (not_56_out, instr[19]);
  not not_57 (not_57_out, instr[18]);
  not not_58 (not_58_out, instr[17]);
  not not_59 (not_59_out, instr[31]);
  not not_60 (not_60_out, instr[30]);
  not not_61 (not_61_out, instr[29]);
  not not_62 (not_62_out, instr[31]);
  not not_63 (not_63_out, instr[30]);
  not not_64 (not_64_out, instr[29]);
  not not_65 (not_65_out, instr[26]);
  not not_66 (not_66_out, instr[31]);
  not not_67 (not_67_out, instr[30]);
  not not_68 (not_68_out, instr[29]);
  not not_69 (not_69_out, instr[28]);
  not not_70 (not_70_out, instr[27]);
  not not_71 (not_71_out, instr[20]);
  not not_72 (not_72_out, instr[19]);
  not not_73 (not_73_out, instr[18]);
  not not_74 (not_74_out, instr[17]);
  not not_75 (not_75_out, instr[16]);
  not not_76 (not_76_out, instr[31]);
  not not_77 (not_77_out, instr[30]);
  not not_78 (not_78_out, instr[29]);
  not not_79 (not_79_out, instr[27]);
  and and_2 (and_2_out, instr[5], not_7_out, not_8_out, not_9_out, not_10_out, instr[0]);
  and and_3 (addiu, not_11_out, not_12_out, instr[3], not_13_out, not_14_out, instr[0]);
  and and_4 (and_4_out, instr[5], not_15_out, not_16_out, instr[2], not_17_out, not_18_out);
  and and_5 (andi, not_19_out, not_20_out, instr[29], instr[28], not_21_out, not_22_out);
  and and_6 (and_6_out, instr[5], not_23_out, not_24_out, not_25_out, instr[1], instr[0]);
  and and_7 (and_7_out, instr[5], not_26_out, not_27_out, instr[2], not_28_out, instr[0]);
  and and_8 (ori, not_29_out, not_30_out, instr[29], instr[28], not_31_out, instr[26]);
  and and_9 (and_9_out, instr[5], not_32_out, not_33_out, instr[2], instr[1], not_34_out);
  and and_10 (xori, not_35_out, not_36_out, instr[29], instr[28], instr[27], not_37_out);
  and and_11 (lui, not_38_out, not_39_out, instr[29], instr[28], instr[27], instr[26]);
  and and_12 (lw, instr[31], not_40_out, not_41_out, not_42_out, instr[27], instr[26]);
  and and_13 (sw, instr[31], not_43_out, instr[29], not_44_out, instr[27], instr[26]);
  and and_14 (beq, not_45_out, not_46_out, not_47_out, instr[28], not_48_out, not_49_out);
  and and_15 (and_15_out, not_50_out, not_51_out, not_52_out, not_53_out, not_54_out, instr[26]);
  and and_16 (and_16_out, not_55_out, not_56_out, not_57_out, not_58_out, instr[16]);
  and and_17 (bgtz, not_59_out, not_60_out, not_61_out, instr[28], instr[27], instr[26]);
  and and_18 (blez, not_62_out, not_63_out, not_64_out, instr[28], instr[27], not_65_out);
  and and_19 (and_19_out, not_66_out, not_67_out, not_68_out, not_69_out, not_70_out, instr[26]);
  and and_20 (and_20_out, not_71_out, not_72_out, not_73_out, not_74_out, not_75_out);
  and and_21 (bne, not_76_out, not_77_out, not_78_out, instr[28], not_79_out, instr[26]);
  and and_22 (addu, and_2_out, opis0);
  and and_23 (\and , and_4_out, opis0);
  and and_24 (subu, and_6_out, opis0);
  and and_25 (\or , and_7_out, opis0);
  and and_26 (\xor , and_9_out, opis0);
  and and_27 (bgez, and_15_out, and_16_out);
  and and_28 (bltz, and_19_out, and_20_out);

  // Other names for the same wires on the sheet: fc1 = instr[0]; fc2 = instr[1]; fc3 = instr[2]; fc4 = instr[3];
  //   fc5 = instr[4]; fc6 = instr[5]; rt1 = instr[16]; rt2 = instr[17]; rt3 = instr[18]; rt4 = instr[19];
  //   rt5 = instr[20]; rs1 = instr[21]; rs2 = instr[22]; rs3 = instr[23]; rs4 = instr[24]; rs5 = instr[25];
  //   op1 = instr[26]; op2 = instr[27]; op3 = instr[28]; op4 = instr[29]; op5 = instr[30]; op6 = instr[31]
endmodule

module ALU (
  input  [31:0] in_1,
  input  [31:0] in_2,
  input  [3:0] ALUOP,
  output Branch,
  output [31:0] Result
);

  wire comparator_1_eq, comparator_2_eq, comparator_2_gt, comparator_2_lt, not_1_out, or_2_out, or_3_out;
  wire [31:0] adder_1_out, and_1_out, or_1_out, shifter_1_out, subtractor_1_out, xor_1_out;

  Adder #(.width(32)) adder_1 (.a(in_1), .b(in_2), .out(adder_1_out));  // open: cin, cout
  Subtractor #(.width(32)) subtractor_1 (.a(in_1), .b(in_2), .out(subtractor_1_out));  // open: bin, bout
  assign and_1_out = in_1 & in_2;  // AND_Gate and_1, 32 bits wide
  assign or_1_out = in_1 | in_2;  // OR_Gate or_1, 32 bits wide
  assign xor_1_out = in_1 ^ in_2;  // XOR_Gate xor_1, 32 bits wide
  Shifter #(.width(32)) shifter_1 (.in(in_2), .\dist (5'b10000), .out(shifter_1_out));
  Comparator #(.width(32)) comparator_1 (.a(in_1), .b(in_2), .eq(comparator_1_eq));  // open: gt, lt
  Comparator #(.width(32)) comparator_2 (
    .a(in_1), .b({32{1'b0}}), .gt(comparator_2_gt), .eq(comparator_2_eq), .lt(comparator_2_lt));
  or or_2 (or_2_out, comparator_2_gt, comparator_2_eq);
  or or_3 (or_3_out, comparator_2_eq, comparator_2_lt);
  not not_1 (not_1_out, comparator_1_eq);
  Multiplexer #(.select(4), .enable("false")) multiplexer_1 (
    .in0(comparator_1_eq), .in1(or_2_out), .in2(comparator_2_gt), .in3(or_3_out), .in4(comparator_2_lt),
    .in5(not_1_out), .out(Branch), .sel(ALUOP));  // open: in6, in7, in8, in9, in10, in11, in12, in13, in14, in15
  Multiplexer #(.select(4), .width(32), .enable("false")) multiplexer_2 (
    .in0(adder_1_out), .in1(subtractor_1_out), .in2(and_1_out), .in3(or_1_out), .in4(xor_1_out),
    .in5(shifter_1_out), .out(Result), .sel(ALUOP));  // open: in6, in7, in8, in9, in10, in11, in12, in13, in14, in15

  // Other names for the same wires on the sheet: A1[31:0] = in_1; A2[31:0] = in_2
endmodule

module or_logic (
  input  addu,
  input  addiu,
  input  \and ,
  input  andi,
  input  subu,
  input  \or ,
  input  ori,
  input  \xor ,
  input  xori,
  input  lui,
  input  lw,
  input  sw,
  input  beq,
  input  bgez,
  input  bgtz,
  input  blez,
  input  bltz,
  input  bne,
  output RegDst,
  output SiExt,
  output Shift2,
  output RegWrite,
  output Rst,
  output ALUSrc,
  output RegIn,
  output MemWrite,
  output Branch_Enable,
  output ALU3,
  output ALU2,
  output ALU1,
  output ALU0
);

  or or_1 (RegDst, andi, ori, lui, lw, xori, sw, addiu);
  buf or_2 (Rst, 1'b0);  // OR_Gate
  or or_3 (Branch_Enable, beq, bgez, bgtz, blez, bltz, bne);
  buf or_4 (ALU3, 1'b0);  // OR_Gate
  or or_5 (SiExt, bgez, bgtz, blez, lw, sw, beq, addiu, bltz, bne);
  or or_6 (ALUSrc, andi, addiu, ori, lui, xori, lw, sw);
  or or_7 (ALU2, lui, xori, \xor , bltz, bne);
  buf or_8 (RegIn, lw);  // OR_Gate
  or or_9 (Shift2, beq, bne, bltz, bgez, bgtz, blez);
  or or_10 (ALU1, ori, \and , andi, blez, \or , bgtz);
  buf or_11 (MemWrite, sw);  // OR_Gate
  or or_12 (ALU0, subu, ori, lui, blez, \or , bgez, bne);
  or or_13 (RegWrite, xori, \xor , andi, \and , addu, addiu, subu, ori, lui, lw, \or );
endmodule

module aa (
  input  addu,
  input  subu,
  input  ori,
  input  lui,
  input  lw,
  input  sw,
  input  beq,
  input  [31:0] in_8,
  output ALU3,
  output ALU2,
  output ALU1,
  output ALU0,
  output [4:0] out_13
);

  wire bitfinder_1_found, not_1_out, not_2_out, not_3_out, not_4_out;

  not not_1 (not_1_out, addu);
  not not_2 (not_2_out, lw);
  not not_3 (not_3_out, sw);
  not not_4 (not_4_out, beq);
  and and_1 (ALU0, not_1_out, not_2_out, not_3_out, not_4_out);
  BitFinder #(.width(32), .\type ("high1")) bitfinder_1 (.in(in_8), .index(out_13), .found(bitfinder_1_found));

  assign ALU1 = ori;
  assign ALU2 = lui;
  assign ALU3 = 1'b0;
endmodule
