// Logisim project 取余.circ as structural Verilog: 5 circuits, main circuit mod5
module mod5 (
  input  in_1,
  output out_2,
  output out_3,
  output out_4,
  output out_5,
  output out_6
);

  wire clock_1_out;
  wire [2:0] a_1_z, register_1_q;

  // Probe on register_1_q
  a a_1 (
    .a(register_1_q[2]), .b(register_1_q[1]), .c(register_1_q[0]), .d(in_1), .x(a_1_z[2]), .y(a_1_z[1]),
    .z(a_1_z[0]));
  Register #(.width(3)) register_1 (.D(a_1_z), .Q(register_1_q), .clk(clock_1_out));  // open: en, clr
  Clock clock_1 (.out(clock_1_out));
  // Probe on a_1_z
  Decoder #(.select(3), .enable("false")) decoder_1 (
    .out0(out_2), .out1(out_3), .out2(out_4), .out3(out_5), .out4(out_6), .sel(a_1_z));  // open: out5, out6, out7
endmodule

module a (
  input  a,
  input  b,
  input  c,
  input  d,
  output x,
  output y,
  output z
);

  wire and_1_out, and_2_out, and_3_out, and_4_out, and_6_out, and_7_out, and_8_out, and_9_out, and_10_out,
       and_11_out, not_1_out, not_2_out, not_3_out, not_4_out, not_5_out, not_6_out, not_7_out, not_8_out,
       not_9_out, not_10_out, not_11_out, not_12_out, or_2_out;

  not not_1 (not_1_out, a);
  and and_1 (and_1_out, not_1_out, b);
  not not_2 (not_2_out, d);
  not not_3 (not_3_out, a);
  not not_4 (not_4_out, b);
  and and_2 (and_2_out, not_4_out, not_5_out);
  not not_5 (not_5_out, c);
  not not_6 (not_6_out, a);
  and and_3 (and_3_out, not_6_out, not_7_out);
  not not_7 (not_7_out, b);
  not not_8 (not_8_out, d);
  not not_9 (not_9_out, b);
  and and_4 (and_4_out, not_9_out, not_10_out);
  not not_10 (not_10_out, c);
  not not_11 (not_11_out, d);
  not not_12 (not_12_out, a);
  and and_5 (x, and_1_out, not_2_out);
  and and_6 (and_6_out, not_3_out, d);
  and and_7 (and_7_out, and_2_out, d);
  and and_8 (and_8_out, and_3_out, not_8_out);
  and and_9 (and_9_out, and_4_out, not_11_out);
  and and_10 (and_10_out, not_12_out, b);
  or or_1 (y, and_6_out, and_7_out);
  or or_2 (or_2_out, and_8_out, and_9_out);
  and and_11 (and_11_out, and_10_out, d);
  or or_3 (z, or_2_out, and_11_out);
endmodule

module \测试  (
  output out_1,
  output out_2,
  output out_3,
  output out_4,
  output out_5,
  output out_6,
  output out_7
);

  wire clock_1_out, undriven, undriven_2;
  wire [3:0] counter_1_q, undriven_3;

  Clock clock_1 (.out(clock_1_out));
  Counter #(.width(4), .max('hf)) counter_1 (
    .load(undriven), .D(undriven_3), .count(undriven_2), .Q(counter_1_q), .carry(out_7), .clk(clock_1_out));  // open: clr
  ROM #(.addrWidth(4), .dataWidth(1)) rom_1 (.addr(counter_1_q), .data(out_1));  // open: sel
  mod5 mod5_1 (.in_1(out_1), .out_2(out_2), .out_3(out_3), .out_4(out_4), .out_5(out_5), .out_6(out_6));

  // Notes on the sheet:
  //   contents of rom_1 (hex, n*v repeats v):
  //   0 1 0 0 1 0 0 1 0 0 1 0 0 1
endmodule

module jcq (
  input  [2:0] in_1,
  input  in_2
);

  wire undriven;
  wire [2:0] register_1_q, xor_1_out;

  // Probe on xor_1_out
  // Probe on register_1_q
  Register #(.width(3)) register_1 (.D(xor_1_out), .Q(register_1_q), .clk(undriven), .clr(in_2));  // open: en
  assign xor_1_out = register_1_q ^ in_1;  // XOR_Gate xor_1, 3 bits wide
endmodule

module rs (
  input  in_1,
  input  in_2,
  output out_3,
  output out_4
);

  wire or_1_out, or_2_out;

  or or_1 (or_1_out, in_1, out_4);
  or or_2 (or_2_out, out_3, in_2);
  not not_1 (out_3, or_1_out);
  not not_2 (out_4, or_2_out);
endmodule
