// Logisim project 斐波那契升级.circ as structural Verilog: 5 circuits, main circuit main
module main (
  input  [31:0] in_1,
  output [31:0] out_2
);

  wire bitselector_1_out, clock_1_out, counter_1_carry, not_1_out, not_2_out, not_3_out, not_4_out,
       not_5_out, not_6_out, register_1_q, register_2_q, register_7_q, register_12_q, xuan;
  wire [5:0] counter_1_q;
  wire [31:0] _1, _2, _3, _4, multiplexer_1_out, register_3_q, register_4_q, register_5_q, register_6_q,
       \两矩阵乘_1_out_9 , \两矩阵乘_1_out_10 , \两矩阵乘_1_out_11 , \两矩阵乘_1_out_12 , \平方_1_out_9 , \平方_1_out_10 ,
       \平方_1_out_11 , \平方_1_out_12 , \选择加法_1_out_5 , \选择加法_2_out_5 , \选择加法_3_out_5 , \选择加法_4_out_5 ;

  Clock clock_1 (.out(clock_1_out));
  Register #(.width(1)) register_1 (.D(not_1_out), .Q(register_1_q), .clk(not_1_out));  // open: en, clr
  Comparator #(.width(32), .mode("unsigned")) comparator_1 (.a({32{1'b0}}), .b(in_1), .eq(xuan));  // open: gt, lt
  BitSelector #(.width(32)) bitselector_1 (.in(in_1), .out(bitselector_1_out), .sel(counter_1_q[4:0]));
  Counter #(.width(6), .max('h20)) counter_1 (
    .Q(counter_1_q), .carry(counter_1_carry), .clk(not_1_out), .clr(not_2_out));  // open: load, D, count
  not not_1 (not_1_out, clock_1_out);
  not not_2 (not_2_out, register_1_q);
  Register #(.width(1)) register_2 (.D(not_1_out), .Q(register_2_q), .clk(not_1_out));  // open: en, clr
  not not_3 (not_3_out, register_2_q);
  \平方  \u_平方_1  (
    .in_1(not_3_out), .in_2(not_3_out), .in_3(not_3_out), .in_5(register_3_q), .in_6(register_4_q),
    .in_7(register_5_q), .in_8(register_6_q), .out_9(\平方_1_out_9 ), .out_10(\平方_1_out_10 ),
    .out_11(\平方_1_out_11 ), .out_12(\平方_1_out_12 ));  // open: in_4
  Register #(.width(32)) register_3 (.D(\平方_1_out_9 ), .Q(register_3_q), .clk(not_1_out));  // open: en, clr
  Register #(.width(32)) register_4 (.D(\平方_1_out_10 ), .Q(register_4_q), .clk(not_1_out));  // open: en, clr
  Register #(.width(32)) register_5 (.D(\平方_1_out_11 ), .Q(register_5_q), .clk(not_1_out));  // open: en, clr
  Register #(.width(32)) register_6 (.D(\平方_1_out_12 ), .Q(register_6_q), .clk(not_1_out));  // open: en, clr
  not not_4 (not_4_out, not_1_out);
  \两矩阵乘  \u_两矩阵乘_1  (
    .in_1(register_3_q), .in_2(register_4_q), .in_3(register_5_q), .in_4(register_6_q), .in_5(_1), .in_6(_2),
    .in_7(_3), .in_8(_4), .out_9(\两矩阵乘_1_out_9 ), .out_10(\两矩阵乘_1_out_10 ), .out_11(\两矩阵乘_1_out_11 ),
    .out_12(\两矩阵乘_1_out_12 ));
  Register #(.width(1)) register_7 (.D(counter_1_carry), .Q(register_7_q), .clk(counter_1_carry));  // open: en, clr
  \选择加法  \u_选择加法_1  (
    .in_1(not_6_out), .in_2(_1), .in_3(\两矩阵乘_1_out_9 ), .in_4(bitselector_1_out), .out_5(\选择加法_1_out_5 ));
  \选择加法  \u_选择加法_2  (
    .in_2(_2), .in_3(\两矩阵乘_1_out_10 ), .in_4(bitselector_1_out), .out_5(\选择加法_2_out_5 ));  // open: in_1
  \选择加法  \u_选择加法_3  (
    .in_2(_3), .in_3(\两矩阵乘_1_out_11 ), .in_4(bitselector_1_out), .out_5(\选择加法_3_out_5 ));  // open: in_1
  \选择加法  \u_选择加法_4  (
    .in_1(not_6_out), .in_2(_4), .in_3(\两矩阵乘_1_out_12 ), .in_4(bitselector_1_out), .out_5(\选择加法_4_out_5 ));
  not not_5 (not_5_out, register_7_q);
  Register #(.width(32)) register_8 (.D(\选择加法_1_out_5 ), .en(not_5_out), .Q(_1), .clk(not_4_out));  // open: clr
  Register #(.width(32)) register_9 (.D(\选择加法_2_out_5 ), .en(not_5_out), .Q(_2), .clk(not_4_out));  // open: clr
  Register #(.width(32)) register_10 (.D(\选择加法_3_out_5 ), .en(not_5_out), .Q(_3), .clk(not_4_out));  // open: clr
  Register #(.width(32)) register_11 (.D(\选择加法_4_out_5 ), .en(not_5_out), .Q(_4), .clk(not_4_out));  // open: clr
  not not_6 (not_6_out, register_12_q);
  Register #(.width(1)) register_12 (.D(not_4_out), .Q(register_12_q), .clk(not_4_out));  // open: en, clr
  Multiplexer #(.width(32)) multiplexer_1 (.in0(_3), .in1(_3), .out(multiplexer_1_out), .sel(xuan));  // open: en
  Multiplexer #(.width(32)) multiplexer_2 (
    .in0({32{1'b0}}), .in1(multiplexer_1_out), .out(out_2), .sel(register_7_q));  // open: en
endmodule

module \两矩阵乘  (
  input  [31:0] in_1,
  input  [31:0] in_2,
  input  [31:0] in_3,
  input  [31:0] in_4,
  input  [31:0] in_5,
  input  [31:0] in_6,
  input  [31:0] in_7,
  input  [31:0] in_8,
  output [31:0] out_9,
  output [31:0] out_10,
  output [31:0] out_11,
  output [31:0] out_12
);

  wire [31:0] multiplier_1_out, multiplier_2_out, multiplier_3_out, multiplier_4_out, multiplier_5_out,
       multiplier_6_out, multiplier_7_out, multiplier_8_out;

  Multiplier #(.width(32)) multiplier_1 (.a(in_1), .b(in_5), .out(multiplier_1_out));  // open: cin, cout
  Multiplier #(.width(32)) multiplier_2 (.a(in_2), .b(in_7), .out(multiplier_2_out));  // open: cin, cout
  Multiplier #(.width(32)) multiplier_3 (.a(in_1), .b(in_6), .out(multiplier_3_out));  // open: cin, cout
  Multiplier #(.width(32)) multiplier_4 (.a(in_2), .b(in_8), .out(multiplier_4_out));  // open: cin, cout
  Multiplier #(.width(32)) multiplier_5 (.a(in_3), .b(in_5), .out(multiplier_5_out));  // open: cin, cout
  Multiplier #(.width(32)) multiplier_6 (.a(in_4), .b(in_7), .out(multiplier_6_out));  // open: cin, cout
  Multiplier #(.width(32)) multiplier_7 (.a(in_3), .b(in_6), .out(multiplier_7_out));  // open: cin, cout
  Multiplier #(.width(32)) multiplier_8 (.a(in_4), .b(in_8), .out(multiplier_8_out));  // open: cin, cout
  Adder #(.width(32)) adder_1 (.a(multiplier_1_out), .b(multiplier_2_out), .out(out_9));  // open: cin, cout
  Adder #(.width(32)) adder_2 (.a(multiplier_3_out), .b(multiplier_4_out), .out(out_10));  // open: cin, cout
  Adder #(.width(32)) adder_3 (.a(multiplier_5_out), .b(multiplier_6_out), .out(out_11));  // open: cin, cout
  Adder #(.width(32)) adder_4 (.a(multiplier_7_out), .b(multiplier_8_out), .out(out_12));  // open: cin, cout
endmodule

module \平方  (
  input  in_1,
  input  in_2,
  input  in_3,
  input  in_4,
  input  [31:0] in_5,
  input  [31:0] in_6,
  input  [31:0] in_7,
  input  [31:0] in_8,
  output [31:0] out_9,
  output [31:0] out_10,
  output [31:0] out_11,
  output [31:0] out_12
);

  wire [31:0] multiplier_1_out, multiplier_2_out, multiplier_3_out, multiplier_4_out, multiplier_5_out,
       multiplier_6_out, multiplier_7_out, multiplier_8_out;

  Multiplier #(.width(32)) multiplier_1 (.a(in_5), .b(in_5), .out(multiplier_1_out));  // open: cin, cout
  Multiplier #(.width(32)) multiplier_2 (.a(in_6), .b(in_7), .out(multiplier_2_out));  // open: cin, cout
  Multiplier #(.width(32)) multiplier_3 (.a(in_5), .b(in_6), .out(multiplier_3_out));  // open: cin, cout
  Multiplier #(.width(32)) multiplier_4 (.a(in_6), .b(in_8), .out(multiplier_4_out));  // open: cin, cout
  Multiplier #(.width(32)) multiplier_5 (.a(in_7), .b(in_5), .out(multiplier_5_out));  // open: cin, cout
  Multiplier #(.width(32)) multiplier_6 (.a(in_8), .b(in_7), .out(multiplier_6_out));  // open: cin, cout
  Multiplier #(.width(32)) multiplier_7 (.a(in_7), .b(in_6), .out(multiplier_7_out));  // open: cin, cout
  Multiplier #(.width(32)) multiplier_8 (.a(in_8), .b(in_8), .out(multiplier_8_out));  // open: cin, cout
  Adder #(.width(32)) adder_1 (.a(multiplier_1_out), .b(multiplier_2_out), .out(out_9), .cin(in_1));  // open: cout
  Adder #(.width(32)) adder_2 (.a(multiplier_3_out), .b(multiplier_4_out), .out(out_10), .cin(in_2));  // open: cout
  Adder #(.width(32)) adder_3 (.a(multiplier_5_out), .b(multiplier_6_out), .out(out_11), .cin(in_3));  // open: cout
  Adder #(.width(32)) adder_4 (.a(multiplier_7_out), .b(multiplier_8_out), .out(out_12), .cin(in_4));  // open: cout
endmodule

module \备用  (
  input  [31:0] in_1
);
endmodule

module \选择加法  (
  input  in_1,
  input  [31:0] in_2,
  input  [31:0] in_3,
  input  in_4,
  output [31:0] out_5
);

  wire [31:0] multiplexer_1_out;

  Multiplexer #(.width(32)) multiplexer_1 (.in0(in_2), .in1(in_3), .out(multiplexer_1_out), .sel(in_4));  // open: en
  Adder #(.width(32)) adder_1 (.a(multiplexer_1_out), .b({32{1'b0}}), .out(out_5), .cin(in_1));  // open: cout
endmodule
