// Logisim project 斐波那契数列.circ as structural Verilog: 6 circuits, main circuit main
module main (
  input  [2:0] in_1,
  output [3:0] out_2
);

  wire clock_1_out, counter_1_carry, multiplexer_1_out, not_1_out, not_2_out, not_3_out, not_4_out,
       not_5_out, not_6_out, not_7_out, register_1_q, register_2_q, register_3_q, register_4_q;
  wire [3:0] adder_1_out, bit_extender_1_out, counter_1_q, not_8_out, register_5_q, register_6_q,
       register_7_q;

  not not_1 (not_1_out, not_2_out);
  // Probe on register_1_q
  Register #(.width(1)) register_1 (.D(not_1_out), .Q(register_1_q), .clk(not_2_out));  // open: en, clr
  not not_2 (not_2_out, not_5_out);
  assign bit_extender_1_out = {{1{1'b0}}, in_1};  // Bit_Extender bit_extender_1
  Register #(.width(1)) register_2 (.D(not_6_out), .Q(register_2_q), .clk(not_6_out));  // open: en, clr
  // Probe on counter_1_q
  Counter #(.width(4), .max('hf)) counter_1 (
    .load(1'b1), .D(bit_extender_1_out), .count(register_1_q), .Q(counter_1_q), .carry(counter_1_carry),
    .clk(not_5_out));  // open: clr
  Multiplexer #(.enable("false")) multiplexer_1 (
    .in0(1'b0), .in1(counter_1_carry), .out(multiplexer_1_out), .sel(register_2_q));
  Register #(.width(1)) register_3 (.D(multiplexer_1_out), .Q(register_3_q), .clk(multiplexer_1_out));  // open: en, clr
  not not_3 (not_3_out, register_3_q);
  Register #(.width(1)) register_4 (.D(not_6_out), .Q(register_4_q), .clk(not_6_out));  // open: en, clr
  not not_4 (not_4_out, register_4_q);
  Adder #(.width(4)) adder_1 (.a(register_6_q), .b(register_7_q), .out(adder_1_out), .cin(not_4_out));  // open: cout
  not not_5 (not_5_out, not_6_out);
  // Probe on register_6_q
  not not_6 (not_6_out, clock_1_out);
  Clock clock_1 (.out(clock_1_out));
  // Probe on adder_1_out
  Register #(.width(4)) register_5 (.D(adder_1_out), .en(not_3_out), .Q(register_5_q), .clk(not_6_out));  // open: clr
  not not_7 (not_7_out, not_6_out);
  // Probe on register_7_q
  Register #(.width(4)) register_6 (.D(register_5_q), .en(not_3_out), .Q(register_6_q), .clk(not_7_out));  // open: clr
  not not_8 (not_8_out[0], 1'b1);
  not not_9 (not_8_out[1], 1'b1);
  not not_10 (not_8_out[3], 1'b1);
  not not_11 (not_8_out[2], 1'b1);
  Register #(.width(4)) register_7 (.D(register_6_q), .en(not_3_out), .Q(register_7_q), .clk(not_6_out));  // open: clr
  Multiplexer #(.width(4)) multiplexer_2 (
    .in0(not_8_out), .in1(register_6_q), .out(out_2), .sel(register_3_q));  // open: en
endmodule

module \测试  (
  input  [2:0] in_1,
  output [3:0] out_2,
  output out_3
);

  wire clock_1_out;
  wire [3:0] undriven;

  main main_1 ();  // open: in_1, out_2
  Clock clock_1 (.out(clock_1_out));
  // Probe on undriven
  Counter counter_1 (.carry(out_3), .clk(clock_1_out));  // open: load, D, count, Q, clr
  Register #(.width(4)) register_1 (.D(undriven), .Q(out_2), .clk(out_3));  // open: en, clr
endmodule

module SR (
  input  in_1
);

  wire register_1_q;

  Register #(.width(1)) register_1 (.D(1'b1), .Q(register_1_q), .clk(in_1), .clr(register_1_q));  // open: en
endmodule

module \备用  (
  input  in_1,
  input  [2:0] in_2,
  output out_3,
  output out_4
);

  wire and_1_out, clock_1_out, clock_2_out, not_1_out, register_1_q;
  wire [2:0] counter_2_q;
  wire [7:0] counter_1_q, xnor_1_out;

  Counter counter_1 (.Q(counter_1_q), .clk(clock_1_out));  // open: load, D, count, carry, clr
  assign xnor_1_out = ~(counter_1_q ^ 8'h23);  // XNOR_Gate xnor_1, 8 bits wide
  Clock clock_1 (.out(clock_1_out));
  RAM #(.bus("separate")) ram_1 (
    .addr(xnor_1_out), .din(counter_1_q), .clk(clock_1_out));  // open: data, str, sel, ld, clr
  Register #(.width(1)) register_1 (.D(not_1_out), .Q(register_1_q), .clk(clock_2_out));  // open: en, clr
  not not_1 (not_1_out, clock_2_out);
  // Probe on register_1_q
  Clock clock_2 (.out(clock_2_out));
  Counter #(.width(3), .max('h7)) counter_2 (
    .load(in_1), .D(in_2), .count(register_1_q), .Q(counter_2_q), .carry(out_3), .clk(clock_2_out),
    .clr(and_1_out));
  and and_1 (and_1_out, out_3, 1'b1);
  // Probe on counter_2_q

  assign out_4 = out_3;
endmodule

module meiyong (
  input  [2:0] in_1
);

  wire clock_1_out, counter_1_carry, not_1_out, not_2_out, register_1_q, register_2_q;
  wire [3:0] bit_extender_1_out, counter_1_q;

  not not_1 (not_1_out, clock_1_out);
  Register #(.width(1)) register_1 (.D(not_1_out), .Q(register_1_q), .clk(clock_1_out));  // open: en, clr
  assign bit_extender_1_out = {{1{1'b0}}, in_1};  // Bit_Extender bit_extender_1
  // Probe on register_1_q
  Clock clock_1 (.out(clock_1_out));
  Counter #(.width(4), .max('hf)) counter_1 (
    .load(1'b1), .D(bit_extender_1_out), .count(register_1_q), .Q(counter_1_q), .carry(counter_1_carry),
    .clk(clock_1_out));  // open: clr
  // Probe on counter_1_q
  not not_2 (not_2_out, register_2_q);
  Register #(.width(1)) register_2 (.D(counter_1_carry), .Q(register_2_q), .clk(counter_1_carry));  // open: en, clr
endmodule

module zhenzhi (
  input  a,
  input  b,
  input  c,
  input  d,
  output w,
  output x,
  output y,
  output z
);


  assign w = c;
  assign x = 1'b0;
  assign y = 1'b0;
  assign z = 1'b1;
endmodule
